// Logisim project 7SegmentDisplay.circ as structural Verilog: 2 circuits, main circuit main
module main (
  input  MSB,
  input  in_2,
  input  in_3,
  input  LSB
);

  wire n7_segment_display_1_a_2, n7_segment_display_1_b_2, n7_segment_display_1_c_2,
       n7_segment_display_1_d_2, n7_segment_display_1_e, n7_segment_display_1_f, n7_segment_display_1_g;

  _7_Segment_Display u_7_segment_display_1 (
    .D(MSB), .C(in_2), .B(in_3), .A(LSB), .a_2(n7_segment_display_1_a_2), .b_2(n7_segment_display_1_b_2),
    .c_2(n7_segment_display_1_c_2), .d_2(n7_segment_display_1_d_2), .e(n7_segment_display_1_e),
    .f(n7_segment_display_1_f), .g(n7_segment_display_1_g));
  _7_Segment_Display_part u_7_segment_display_2 (
    .g(n7_segment_display_1_g), .f(n7_segment_display_1_f), .a(n7_segment_display_1_a_2),
    .b(n7_segment_display_1_b_2), .e(n7_segment_display_1_e), .d(n7_segment_display_1_d_2),
    .c(n7_segment_display_1_c_2));  // open: dp
endmodule

module _7_Segment_Display (
  input  D,
  input  C,
  input  B,
  input  A,
  output a_2,
  output b_2,
  output c_2,
  output d_2,
  output e,
  output f,
  output g
);

  wire and_1_out, and_2_out, and_3_out, and_4_out, and_5_out, and_6_out, and_7_out, and_8_out, and_9_out,
       and_10_out, and_11_out, and_12_out, and_13_out, and_14_out, and_15_out, and_16_out, and_17_out,
       not_1_out, not_2_out, not_3_out, not_4_out, not_5_out, not_6_out, not_7_out, not_8_out, not_9_out,
       not_10_out, not_11_out, not_12_out, not_13_out, not_14_out, not_15_out, not_16_out, not_17_out,
       not_18_out, not_19_out, not_20_out, not_21_out, or_1_out, or_2_out, or_3_out, or_4_out, or_6_out,
       or_8_out, or_9_out, or_10_out, or_11_out, or_14_out, or_15_out;

  not not_1 (not_1_out, C);
  and and_1 (and_1_out, not_1_out, not_2_out);
  not not_2 (not_2_out, A);
  and and_2 (and_2_out, C, A);
  not not_3 (not_3_out, C);
  not not_4 (not_4_out, B);
  and and_3 (and_3_out, not_4_out, not_5_out);
  not not_5 (not_5_out, A);
  not not_6 (not_6_out, B);
  or or_1 (or_1_out, not_6_out, A);
  not not_7 (not_7_out, C);
  and and_4 (and_4_out, not_7_out, not_8_out);
  not not_8 (not_8_out, A);
  not not_9 (not_9_out, C);
  and and_5 (and_5_out, not_9_out, B);
  not not_10 (not_10_out, A);
  and and_6 (and_6_out, C, not_11_out);
  not not_11 (not_11_out, B);
  not not_12 (not_12_out, C);
  and and_7 (and_7_out, not_12_out, not_13_out);
  not not_13 (not_13_out, A);
  and and_8 (and_8_out, B, not_14_out);
  not not_14 (not_14_out, A);
  not not_15 (not_15_out, B);
  and and_9 (and_9_out, not_15_out, not_16_out);
  not not_16 (not_16_out, A);
  and and_10 (and_10_out, C, not_17_out);
  not not_17 (not_17_out, B);
  and and_11 (and_11_out, C, not_18_out);
  not not_18 (not_18_out, A);
  not not_19 (not_19_out, C);
  and and_12 (and_12_out, not_19_out, B);
  and and_13 (and_13_out, C, not_20_out);
  not not_20 (not_20_out, B);
  and and_14 (and_14_out, C, not_21_out);
  not not_21 (not_21_out, A);
  or or_2 (or_2_out, and_1_out, B);
  or or_3 (or_3_out, and_2_out, D);
  or or_4 (or_4_out, not_3_out, and_3_out);
  and and_15 (and_15_out, B, A);
  or or_5 (c_2, or_1_out, C);
  or or_6 (or_6_out, and_4_out, and_5_out);
  and and_16 (and_16_out, B, not_10_out);
  and and_17 (and_17_out, and_6_out, A);
  or or_7 (e, and_7_out, and_8_out);
  or or_8 (or_8_out, and_9_out, and_10_out);
  or or_9 (or_9_out, and_11_out, D);
  or or_10 (or_10_out, and_12_out, and_13_out);
  or or_11 (or_11_out, and_14_out, D);
  or or_12 (a_2, or_2_out, or_3_out);
  or or_13 (b_2, or_4_out, and_15_out);
  or or_14 (or_14_out, or_6_out, and_16_out);
  or or_15 (or_15_out, and_17_out, D);
  or or_16 (f, or_8_out, or_9_out);
  or or_17 (g, or_10_out, or_11_out);
  or or_18 (d_2, or_14_out, or_15_out);
endmodule
