// Logisim project Project.circ as structural Verilog: 11 circuits, main circuit main
module main (
  input  [3:0] a4,
  input  [3:0] a3,
  input  [3:0] a2,
  input  [3:0] a1,
  input  [3:0] b4,
  input  [3:0] b3,
  input  [3:0] b2,
  input  [3:0] b1,
  input  [3:0] a2_2,
  input  [3:0] a1_2,
  input  [3:0] a4_2,
  input  [3:0] a3_2,
  input  [3:0] b4_2,
  input  [3:0] b3_2,
  input  [3:0] b2_2,
  input  [3:0] b1_2,
  input  [3:0] a1_3,
  input  [3:0] a2_3,
  input  [3:0] a3_3,
  input  [3:0] a4_3,
  input  [3:0] Scalar,
  input  [3:0] a1_4,
  input  [3:0] a2_4,
  input  [3:0] a3_4,
  input  [3:0] a4_4,
  input  [3:0] a1_5,
  input  [3:0] a2_5,
  input  [3:0] a3_5,
  input  [3:0] a4_5,
  input  [3:0] b1_3,
  input  [3:0] b2_3,
  input  [3:0] b3_3,
  input  [3:0] b4_3,
  input  [3:0] a1_6,
  input  [3:0] a2_6,
  input  [3:0] a3_6,
  input  [3:0] a4_6,
  input  [3:0] a1_7,
  input  [3:0] a2_7,
  input  [3:0] a3_7,
  input  [3:0] a4_7
);

  wire determinant_1_out_6, inverse_1_nb2, inverse_1_nb3, n7segment_1_a_2, n7segment_1_b_2, n7segment_1_c_2,
       n7segment_1_d_2, n7segment_1_e, n7segment_1_f, n7segment_1_g, n7segment_2_a_2, n7segment_2_b_2,
       n7segment_2_c_2, n7segment_2_d_2, n7segment_2_e, n7segment_2_f, n7segment_2_g, n7segment_3_a_2,
       n7segment_3_b_2, n7segment_3_c_2, n7segment_3_d_2, n7segment_3_e, n7segment_3_f, n7segment_3_g,
       n7segment_4_a_2, n7segment_4_b_2, n7segment_4_c_2, n7segment_4_d_2, n7segment_4_e, n7segment_4_f,
       n7segment_4_g, n7segment_5_a_2, n7segment_5_b_2, n7segment_5_c_2, n7segment_5_d_2, n7segment_5_e,
       n7segment_5_f, n7segment_5_g, n7segment_6_a_2, n7segment_6_b_2, n7segment_6_c_2, n7segment_6_d_2,
       n7segment_6_e, n7segment_6_f, n7segment_6_g, n7segment_7_a_2, n7segment_7_b_2, n7segment_7_c_2,
       n7segment_7_d_2, n7segment_7_e, n7segment_7_f, n7segment_7_g, n7segment_8_a_2, n7segment_8_b_2,
       n7segment_8_c_2, n7segment_8_d_2, n7segment_8_e, n7segment_8_f, n7segment_8_g, n7segment_9_a_2,
       n7segment_9_b_2, n7segment_9_c_2, n7segment_9_d_2, n7segment_9_e, n7segment_9_f, n7segment_9_g,
       n7segment_10_a_2, n7segment_10_b_2, n7segment_10_c_2, n7segment_10_d_2, n7segment_10_e,
       n7segment_10_f, n7segment_10_g, n7segment_11_a_2, n7segment_11_b_2, n7segment_11_c_2,
       n7segment_11_d_2, n7segment_11_e, n7segment_11_f, n7segment_11_g, n7segment_12_a_2, n7segment_12_b_2,
       n7segment_12_c_2, n7segment_12_d_2, n7segment_12_e, n7segment_12_f, n7segment_12_g, n7segment_13_a_2,
       n7segment_13_b_2, n7segment_13_c_2, n7segment_13_d_2, n7segment_13_e, n7segment_13_f, n7segment_13_g,
       n7segment_14_a_2, n7segment_14_b_2, n7segment_14_c_2, n7segment_14_d_2, n7segment_14_e,
       n7segment_14_f, n7segment_14_g, n7segment_15_a_2, n7segment_15_b_2, n7segment_15_c_2,
       n7segment_15_d_2, n7segment_15_e, n7segment_15_f, n7segment_15_g, n7segment_16_a_2, n7segment_16_b_2,
       n7segment_16_c_2, n7segment_16_d_2, n7segment_16_e, n7segment_16_f, n7segment_16_g, n7segment_17_a_2,
       n7segment_17_b_2, n7segment_17_c_2, n7segment_17_d_2, n7segment_17_e, n7segment_17_f, n7segment_17_g,
       n7segment_18_a_2, n7segment_18_b_2, n7segment_18_c_2, n7segment_18_d_2, n7segment_18_e,
       n7segment_18_f, n7segment_18_g, n7segment_19_a_2, n7segment_19_b_2, n7segment_19_c_2,
       n7segment_19_d_2, n7segment_19_e, n7segment_19_f, n7segment_19_g, n7segment_20_a_2, n7segment_20_b_2,
       n7segment_20_c_2, n7segment_20_d_2, n7segment_20_e, n7segment_20_f, n7segment_20_g, n7segment_21_a_2,
       n7segment_21_b_2, n7segment_21_c_2, n7segment_21_d_2, n7segment_21_e, n7segment_21_f, n7segment_21_g,
       n7segment_22_a_2, n7segment_22_b_2, n7segment_22_c_2, n7segment_22_d_2, n7segment_22_e,
       n7segment_22_f, n7segment_22_g, n7segment_23_a_2, n7segment_23_b_2, n7segment_23_c_2,
       n7segment_23_d_2, n7segment_23_e, n7segment_23_f, n7segment_23_g, n7segment_24_a_2, n7segment_24_b_2,
       n7segment_24_c_2, n7segment_24_d_2, n7segment_24_e, n7segment_24_f, n7segment_24_g, n7segment_25_a_2,
       n7segment_25_b_2, n7segment_25_c_2, n7segment_25_d_2, n7segment_25_e, n7segment_25_f, n7segment_25_g,
       sub_1_out_10, sub_1_out_12, sub_1_out_14, sub_1_out_16;
  wire [3:0] adder_1_c1, adder_1_c2, adder_1_c3, adder_1_c4, determinant_1_out_5, inverse_1_b1, inverse_1_b2,
       inverse_1_b3, inverse_1_b4, matrix_mulitplier_1_out_9, matrix_mulitplier_1_out_10,
       matrix_mulitplier_1_out_11, matrix_mulitplier_1_out_12, scalar_multiplier_1_out_6,
       scalar_multiplier_1_out_7, scalar_multiplier_1_out_8, scalar_multiplier_1_out_9, sub_1_out_9,
       sub_1_out_11, sub_1_out_13, sub_1_out_15, transpose_1_out_5, transpose_1_out_6, transpose_1_out_7,
       transpose_1_out_8;

  Adder adder_1 (
    .a1(a1), .b1(b1), .a2(a2), .b2(b2), .a3(a3), .b3(b3), .a4(a4), .b4(b4), .c1(adder_1_c1), .c2(adder_1_c2),
    .c3(adder_1_c3), .c4(adder_1_c4));
  Scalar_multiplier scalar_multiplier_1 (
    .in_1(Scalar), .in_2(a1_4), .in_3(a2_4), .in_4(a3_4), .in_5(a4_4), .out_6(scalar_multiplier_1_out_6),
    .out_7(scalar_multiplier_1_out_7), .out_8(scalar_multiplier_1_out_8), .out_9(scalar_multiplier_1_out_9));
  Matrix_Mulitplier matrix_mulitplier_1 (
    .a1(a1_5), .a2(a2_5), .a3(a3_5), .a4(a4_5), .b1(b1_3), .b2(b2_3), .b3(b3_3), .b4(b4_3),
    .out_9(matrix_mulitplier_1_out_9), .out_10(matrix_mulitplier_1_out_10),
    .out_11(matrix_mulitplier_1_out_11), .out_12(matrix_mulitplier_1_out_12));
  Transpose transpose_1 (
    .a1(a1_6), .out_6(transpose_1_out_6), .a2(a2_6), .a3(a3_6), .a4(a4_6), .out_5(transpose_1_out_5),
    .out_7(transpose_1_out_7), .out_8(transpose_1_out_8));
  Inverse inverse_1 (
    .a1(a1_7), .a2(a2_7), .a3(a3_7), .a4(a4_7), .b1(inverse_1_b1), .b2(inverse_1_b2), .b3(inverse_1_b3),
    .b4(inverse_1_b4), .nb2(inverse_1_nb2), .nb3(inverse_1_nb3));
  Determinant determinant_1 (
    .a1(a1_3), .a2(a2_3), .a3(a3_3), .a4(a4_3), .out_5(determinant_1_out_5), .out_6(determinant_1_out_6));
  Sub sub_1 (
    .out_9(sub_1_out_9), .a1(a1_2), .b1(b1_2), .out_10(sub_1_out_10), .out_11(sub_1_out_11), .a2(a2_2),
    .b2(b2_2), .out_12(sub_1_out_12), .out_13(sub_1_out_13), .a3(a3_2), .b3(b3_2), .out_14(sub_1_out_14),
    .out_15(sub_1_out_15), .a4(a4_2), .b4(b4_2), .out_16(sub_1_out_16));
  _7_Segment_Display u_7_segment_display_1 (
    .g(n7segment_9_g), .f(n7segment_9_f), .a(n7segment_9_a_2), .b(n7segment_9_b_2), .e(n7segment_9_e),
    .d(n7segment_9_d_2), .c(n7segment_9_c_2));  // open: dp
  _7_Segment_Display u_7_segment_display_2 (
    .g(n7segment_10_g), .f(n7segment_10_f), .a(n7segment_10_a_2), .b(n7segment_10_b_2), .e(n7segment_10_e),
    .d(n7segment_10_d_2), .c(n7segment_10_c_2));  // open: dp
  _7_Segment_Display u_7_segment_display_3 (.g(inverse_1_nb3));  // open: f, a, b, e, d, c, dp
  _7segment u_7segment_1 (
    .D(adder_1_c1[3]), .C(adder_1_c1[2]), .B(adder_1_c1[1]), .A(adder_1_c1[0]), .a_2(n7segment_1_a_2),
    .b_2(n7segment_1_b_2), .c_2(n7segment_1_c_2), .d_2(n7segment_1_d_2), .e(n7segment_1_e),
    .f(n7segment_1_f), .g(n7segment_1_g));
  _7segment u_7segment_2 (
    .D(adder_1_c3[3]), .C(adder_1_c3[2]), .B(adder_1_c3[1]), .A(adder_1_c3[0]), .a_2(n7segment_2_a_2),
    .b_2(n7segment_2_b_2), .c_2(n7segment_2_c_2), .d_2(n7segment_2_d_2), .e(n7segment_2_e),
    .f(n7segment_2_f), .g(n7segment_2_g));
  _7_Segment_Display u_7_segment_display_4 (.g(sub_1_out_10));  // open: f, a, b, e, d, c, dp
  _7_Segment_Display u_7_segment_display_5 (
    .g(n7segment_11_g), .f(n7segment_11_f), .a(n7segment_11_a_2), .b(n7segment_11_b_2), .e(n7segment_11_e),
    .d(n7segment_11_d_2), .c(n7segment_11_c_2));  // open: dp
  _7_Segment_Display u_7_segment_display_6 (.g(sub_1_out_14));  // open: f, a, b, e, d, c, dp
  _7_Segment_Display u_7_segment_display_7 (
    .g(n7segment_12_g), .f(n7segment_12_f), .a(n7segment_12_a_2), .b(n7segment_12_b_2), .e(n7segment_12_e),
    .d(n7segment_12_d_2), .c(n7segment_12_c_2));  // open: dp
  _7segment u_7segment_3 (
    .D(scalar_multiplier_1_out_6[3]), .C(scalar_multiplier_1_out_6[2]), .B(scalar_multiplier_1_out_6[1]),
    .A(scalar_multiplier_1_out_6[0]), .a_2(n7segment_3_a_2), .b_2(n7segment_3_b_2), .c_2(n7segment_3_c_2),
    .d_2(n7segment_3_d_2), .e(n7segment_3_e), .f(n7segment_3_f), .g(n7segment_3_g));
  _7segment u_7segment_4 (
    .D(scalar_multiplier_1_out_8[3]), .C(scalar_multiplier_1_out_8[2]), .B(scalar_multiplier_1_out_8[1]),
    .A(scalar_multiplier_1_out_8[0]), .a_2(n7segment_4_a_2), .b_2(n7segment_4_b_2), .c_2(n7segment_4_c_2),
    .d_2(n7segment_4_d_2), .e(n7segment_4_e), .f(n7segment_4_f), .g(n7segment_4_g));
  _7segment u_7segment_5 (
    .D(matrix_mulitplier_1_out_9[3]), .C(matrix_mulitplier_1_out_9[2]), .B(matrix_mulitplier_1_out_9[1]),
    .A(matrix_mulitplier_1_out_9[0]), .a_2(n7segment_5_a_2), .b_2(n7segment_5_b_2), .c_2(n7segment_5_c_2),
    .d_2(n7segment_5_d_2), .e(n7segment_5_e), .f(n7segment_5_f), .g(n7segment_5_g));
  _7segment u_7segment_6 (
    .D(matrix_mulitplier_1_out_11[3]), .C(matrix_mulitplier_1_out_11[2]), .B(matrix_mulitplier_1_out_11[1]),
    .A(matrix_mulitplier_1_out_11[0]), .a_2(n7segment_6_a_2), .b_2(n7segment_6_b_2), .c_2(n7segment_6_c_2),
    .d_2(n7segment_6_d_2), .e(n7segment_6_e), .f(n7segment_6_f), .g(n7segment_6_g));
  _7segment u_7segment_7 (
    .D(transpose_1_out_5[3]), .C(transpose_1_out_5[2]), .B(transpose_1_out_5[1]), .A(transpose_1_out_5[0]),
    .a_2(n7segment_7_a_2), .b_2(n7segment_7_b_2), .c_2(n7segment_7_c_2), .d_2(n7segment_7_d_2),
    .e(n7segment_7_e), .f(n7segment_7_f), .g(n7segment_7_g));
  _7segment u_7segment_8 (
    .D(transpose_1_out_7[3]), .C(transpose_1_out_7[2]), .B(transpose_1_out_7[1]), .A(transpose_1_out_7[0]),
    .a_2(n7segment_8_a_2), .b_2(n7segment_8_b_2), .c_2(n7segment_8_c_2), .d_2(n7segment_8_d_2),
    .e(n7segment_8_e), .f(n7segment_8_f), .g(n7segment_8_g));
  _7segment u_7segment_9 (
    .D(inverse_1_b1[3]), .C(inverse_1_b1[2]), .B(inverse_1_b1[1]), .A(inverse_1_b1[0]),
    .a_2(n7segment_9_a_2), .b_2(n7segment_9_b_2), .c_2(n7segment_9_c_2), .d_2(n7segment_9_d_2),
    .e(n7segment_9_e), .f(n7segment_9_f), .g(n7segment_9_g));
  _7segment u_7segment_10 (
    .D(inverse_1_b3[3]), .C(inverse_1_b3[2]), .B(inverse_1_b3[1]), .A(inverse_1_b3[0]),
    .a_2(n7segment_10_a_2), .b_2(n7segment_10_b_2), .c_2(n7segment_10_c_2), .d_2(n7segment_10_d_2),
    .e(n7segment_10_e), .f(n7segment_10_f), .g(n7segment_10_g));
  _7_Segment_Display u_7_segment_display_8 (
    .g(n7segment_13_g), .f(n7segment_13_f), .a(n7segment_13_a_2), .b(n7segment_13_b_2), .e(n7segment_13_e),
    .d(n7segment_13_d_2), .c(n7segment_13_c_2));  // open: dp
  _7_Segment_Display u_7_segment_display_9 (.g(determinant_1_out_6));  // open: f, a, b, e, d, c, dp
  _7_Segment_Display u_7_segment_display_10 (
    .g(n7segment_1_g), .f(n7segment_1_f), .a(n7segment_1_a_2), .b(n7segment_1_b_2), .e(n7segment_1_e),
    .d(n7segment_1_d_2), .c(n7segment_1_c_2));  // open: dp
  _7_Segment_Display u_7_segment_display_11 (
    .g(n7segment_2_g), .f(n7segment_2_f), .a(n7segment_2_a_2), .b(n7segment_2_b_2), .e(n7segment_2_e),
    .d(n7segment_2_d_2), .c(n7segment_2_c_2));  // open: dp
  _7segment u_7segment_11 (
    .D(sub_1_out_9[3]), .C(sub_1_out_9[2]), .B(sub_1_out_9[1]), .A(sub_1_out_9[0]), .a_2(n7segment_11_a_2),
    .b_2(n7segment_11_b_2), .c_2(n7segment_11_c_2), .d_2(n7segment_11_d_2), .e(n7segment_11_e),
    .f(n7segment_11_f), .g(n7segment_11_g));
  _7segment u_7segment_12 (
    .D(sub_1_out_13[3]), .C(sub_1_out_13[2]), .B(sub_1_out_13[1]), .A(sub_1_out_13[0]),
    .a_2(n7segment_12_a_2), .b_2(n7segment_12_b_2), .c_2(n7segment_12_c_2), .d_2(n7segment_12_d_2),
    .e(n7segment_12_e), .f(n7segment_12_f), .g(n7segment_12_g));
  _7_Segment_Display u_7_segment_display_12 (
    .g(n7segment_3_g), .f(n7segment_3_f), .a(n7segment_3_a_2), .b(n7segment_3_b_2), .e(n7segment_3_e),
    .d(n7segment_3_d_2), .c(n7segment_3_c_2));  // open: dp
  _7_Segment_Display u_7_segment_display_13 (
    .g(n7segment_4_g), .f(n7segment_4_f), .a(n7segment_4_a_2), .b(n7segment_4_b_2), .e(n7segment_4_e),
    .d(n7segment_4_d_2), .c(n7segment_4_c_2));  // open: dp
  _7_Segment_Display u_7_segment_display_14 (
    .g(n7segment_5_g), .f(n7segment_5_f), .a(n7segment_5_a_2), .b(n7segment_5_b_2), .e(n7segment_5_e),
    .d(n7segment_5_d_2), .c(n7segment_5_c_2));  // open: dp
  _7_Segment_Display u_7_segment_display_15 (
    .g(n7segment_6_g), .f(n7segment_6_f), .a(n7segment_6_a_2), .b(n7segment_6_b_2), .e(n7segment_6_e),
    .d(n7segment_6_d_2), .c(n7segment_6_c_2));  // open: dp
  _7_Segment_Display u_7_segment_display_16 (
    .g(n7segment_7_g), .f(n7segment_7_f), .a(n7segment_7_a_2), .b(n7segment_7_b_2), .e(n7segment_7_e),
    .d(n7segment_7_d_2), .c(n7segment_7_c_2));  // open: dp
  _7_Segment_Display u_7_segment_display_17 (
    .g(n7segment_8_g), .f(n7segment_8_f), .a(n7segment_8_a_2), .b(n7segment_8_b_2), .e(n7segment_8_e),
    .d(n7segment_8_d_2), .c(n7segment_8_c_2));  // open: dp
  _7segment u_7segment_13 (
    .D(determinant_1_out_5[3]), .C(determinant_1_out_5[2]), .B(determinant_1_out_5[1]),
    .A(determinant_1_out_5[0]), .a_2(n7segment_13_a_2), .b_2(n7segment_13_b_2), .c_2(n7segment_13_c_2),
    .d_2(n7segment_13_d_2), .e(n7segment_13_e), .f(n7segment_13_f), .g(n7segment_13_g));
  _7_Segment_Display u_7_segment_display_18 (.g(inverse_1_nb2));  // open: f, a, b, e, d, c, dp
  _7_Segment_Display u_7_segment_display_19 (
    .g(n7segment_22_g), .f(n7segment_22_f), .a(n7segment_22_a_2), .b(n7segment_22_b_2), .e(n7segment_22_e),
    .d(n7segment_22_d_2), .c(n7segment_22_c_2));  // open: dp
  _7_Segment_Display u_7_segment_display_20 (
    .g(n7segment_23_g), .f(n7segment_23_f), .a(n7segment_23_a_2), .b(n7segment_23_b_2), .e(n7segment_23_e),
    .d(n7segment_23_d_2), .c(n7segment_23_c_2));  // open: dp
  _7_Segment_Display u_7_segment_display_21 (
    .g(n7segment_24_g), .f(n7segment_24_f), .a(n7segment_24_a_2), .b(n7segment_24_b_2), .e(n7segment_24_e),
    .d(n7segment_24_d_2), .c(n7segment_24_c_2));  // open: dp
  _7_Segment_Display u_7_segment_display_22 (.g(sub_1_out_12));  // open: f, a, b, e, d, c, dp
  _7_Segment_Display u_7_segment_display_23 (.g(sub_1_out_16));  // open: f, a, b, e, d, c, dp
  _7_Segment_Display u_7_segment_display_24 (
    .g(n7segment_25_g), .f(n7segment_25_f), .a(n7segment_25_a_2), .b(n7segment_25_b_2), .e(n7segment_25_e),
    .d(n7segment_25_d_2), .c(n7segment_25_c_2));  // open: dp
  _7segment u_7segment_14 (
    .D(adder_1_c2[3]), .C(adder_1_c2[2]), .B(adder_1_c2[1]), .A(adder_1_c2[0]), .a_2(n7segment_14_a_2),
    .b_2(n7segment_14_b_2), .c_2(n7segment_14_c_2), .d_2(n7segment_14_d_2), .e(n7segment_14_e),
    .f(n7segment_14_f), .g(n7segment_14_g));
  _7segment u_7segment_15 (
    .D(adder_1_c4[3]), .C(adder_1_c4[2]), .B(adder_1_c4[1]), .A(adder_1_c4[0]), .a_2(n7segment_15_a_2),
    .b_2(n7segment_15_b_2), .c_2(n7segment_15_c_2), .d_2(n7segment_15_d_2), .e(n7segment_15_e),
    .f(n7segment_15_f), .g(n7segment_15_g));
  _7segment u_7segment_16 (
    .D(scalar_multiplier_1_out_7[3]), .C(scalar_multiplier_1_out_7[2]), .B(scalar_multiplier_1_out_7[1]),
    .A(scalar_multiplier_1_out_7[0]), .a_2(n7segment_16_a_2), .b_2(n7segment_16_b_2), .c_2(n7segment_16_c_2),
    .d_2(n7segment_16_d_2), .e(n7segment_16_e), .f(n7segment_16_f), .g(n7segment_16_g));
  _7segment u_7segment_17 (
    .D(scalar_multiplier_1_out_9[3]), .C(scalar_multiplier_1_out_9[2]), .B(scalar_multiplier_1_out_9[1]),
    .A(scalar_multiplier_1_out_9[0]), .a_2(n7segment_17_a_2), .b_2(n7segment_17_b_2), .c_2(n7segment_17_c_2),
    .d_2(n7segment_17_d_2), .e(n7segment_17_e), .f(n7segment_17_f), .g(n7segment_17_g));
  _7segment u_7segment_18 (
    .D(matrix_mulitplier_1_out_10[3]), .C(matrix_mulitplier_1_out_10[2]), .B(matrix_mulitplier_1_out_10[1]),
    .A(matrix_mulitplier_1_out_10[0]), .a_2(n7segment_18_a_2), .b_2(n7segment_18_b_2),
    .c_2(n7segment_18_c_2), .d_2(n7segment_18_d_2), .e(n7segment_18_e), .f(n7segment_18_f), .g(n7segment_18_g));
  _7segment u_7segment_19 (
    .D(matrix_mulitplier_1_out_12[3]), .C(matrix_mulitplier_1_out_12[2]), .B(matrix_mulitplier_1_out_12[1]),
    .A(matrix_mulitplier_1_out_12[0]), .a_2(n7segment_19_a_2), .b_2(n7segment_19_b_2),
    .c_2(n7segment_19_c_2), .d_2(n7segment_19_d_2), .e(n7segment_19_e), .f(n7segment_19_f), .g(n7segment_19_g));
  _7segment u_7segment_20 (
    .D(transpose_1_out_6[3]), .C(transpose_1_out_6[2]), .B(transpose_1_out_6[1]), .A(transpose_1_out_6[0]),
    .a_2(n7segment_20_a_2), .b_2(n7segment_20_b_2), .c_2(n7segment_20_c_2), .d_2(n7segment_20_d_2),
    .e(n7segment_20_e), .f(n7segment_20_f), .g(n7segment_20_g));
  _7segment u_7segment_21 (
    .D(transpose_1_out_8[3]), .C(transpose_1_out_8[2]), .B(transpose_1_out_8[1]), .A(transpose_1_out_8[0]),
    .a_2(n7segment_21_a_2), .b_2(n7segment_21_b_2), .c_2(n7segment_21_c_2), .d_2(n7segment_21_d_2),
    .e(n7segment_21_e), .f(n7segment_21_f), .g(n7segment_21_g));
  _7segment u_7segment_22 (
    .D(inverse_1_b2[3]), .C(inverse_1_b2[2]), .B(inverse_1_b2[1]), .A(inverse_1_b2[0]),
    .a_2(n7segment_22_a_2), .b_2(n7segment_22_b_2), .c_2(n7segment_22_c_2), .d_2(n7segment_22_d_2),
    .e(n7segment_22_e), .f(n7segment_22_f), .g(n7segment_22_g));
  _7segment u_7segment_23 (
    .D(inverse_1_b4[3]), .C(inverse_1_b4[2]), .B(inverse_1_b4[1]), .A(inverse_1_b4[0]),
    .a_2(n7segment_23_a_2), .b_2(n7segment_23_b_2), .c_2(n7segment_23_c_2), .d_2(n7segment_23_d_2),
    .e(n7segment_23_e), .f(n7segment_23_f), .g(n7segment_23_g));
  _7segment u_7segment_24 (
    .D(sub_1_out_11[3]), .C(sub_1_out_11[2]), .B(sub_1_out_11[1]), .A(sub_1_out_11[0]),
    .a_2(n7segment_24_a_2), .b_2(n7segment_24_b_2), .c_2(n7segment_24_c_2), .d_2(n7segment_24_d_2),
    .e(n7segment_24_e), .f(n7segment_24_f), .g(n7segment_24_g));
  _7segment u_7segment_25 (
    .D(sub_1_out_15[3]), .C(sub_1_out_15[2]), .B(sub_1_out_15[1]), .A(sub_1_out_15[0]),
    .a_2(n7segment_25_a_2), .b_2(n7segment_25_b_2), .c_2(n7segment_25_c_2), .d_2(n7segment_25_d_2),
    .e(n7segment_25_e), .f(n7segment_25_f), .g(n7segment_25_g));
  _7_Segment_Display u_7_segment_display_25 (
    .g(n7segment_14_g), .f(n7segment_14_f), .a(n7segment_14_a_2), .b(n7segment_14_b_2), .e(n7segment_14_e),
    .d(n7segment_14_d_2), .c(n7segment_14_c_2));  // open: dp
  _7_Segment_Display u_7_segment_display_26 (
    .g(n7segment_15_g), .f(n7segment_15_f), .a(n7segment_15_a_2), .b(n7segment_15_b_2), .e(n7segment_15_e),
    .d(n7segment_15_d_2), .c(n7segment_15_c_2));  // open: dp
  _7_Segment_Display u_7_segment_display_27 (
    .g(n7segment_19_g), .f(n7segment_19_f), .a(n7segment_19_a_2), .b(n7segment_19_b_2), .e(n7segment_19_e),
    .d(n7segment_19_d_2), .c(n7segment_19_c_2));  // open: dp
  _7_Segment_Display u_7_segment_display_28 (
    .g(n7segment_20_g), .f(n7segment_20_f), .a(n7segment_20_a_2), .b(n7segment_20_b_2), .e(n7segment_20_e),
    .d(n7segment_20_d_2), .c(n7segment_20_c_2));  // open: dp
  _7_Segment_Display u_7_segment_display_29 (
    .g(n7segment_21_g), .f(n7segment_21_f), .a(n7segment_21_a_2), .b(n7segment_21_b_2), .e(n7segment_21_e),
    .d(n7segment_21_d_2), .c(n7segment_21_c_2));  // open: dp
  _7_Segment_Display u_7_segment_display_30 (
    .g(n7segment_16_g), .f(n7segment_16_f), .a(n7segment_16_a_2), .b(n7segment_16_b_2), .e(n7segment_16_e),
    .d(n7segment_16_d_2), .c(n7segment_16_c_2));  // open: dp
  _7_Segment_Display u_7_segment_display_31 (
    .g(n7segment_17_g), .f(n7segment_17_f), .a(n7segment_17_a_2), .b(n7segment_17_b_2), .e(n7segment_17_e),
    .d(n7segment_17_d_2), .c(n7segment_17_c_2));  // open: dp
  _7_Segment_Display u_7_segment_display_32 (
    .g(n7segment_18_g), .f(n7segment_18_f), .a(n7segment_18_a_2), .b(n7segment_18_b_2), .e(n7segment_18_e),
    .d(n7segment_18_d_2), .c(n7segment_18_c_2));  // open: dp

  // Notes on the sheet:
  //   a1
  //   a3
  //   Matrix of the form:
  //   a2
  //   a4
  //   For inverse i havent yet added the not existing case
  //   Transpose:
  //   a1
  //   a2
  //   a3
  //   a4
endmodule

module Adder (
  input  [3:0] a1,
  input  [3:0] b1,
  input  [3:0] a2,
  input  [3:0] b2,
  input  [3:0] a3,
  input  [3:0] b3,
  input  [3:0] a4,
  input  [3:0] b4,
  output [3:0] c1,
  output [3:0] c2,
  output [3:0] c3,
  output [3:0] c4
);

  Adder_part #(.width(4)) adder_1 (.a(a1), .b(b1), .out(c1));  // open: cin, cout
  Adder_part #(.width(4)) adder_2 (.a(a2), .b(b2), .out(c2));  // open: cin, cout
  Adder_part #(.width(4)) adder_3 (.a(a3), .b(b3), .out(c3));  // open: cin, cout
  Adder_part #(.width(4)) adder_4 (.a(a4), .b(b4), .out(c4));  // open: cin, cout
endmodule

module Determinant (
  input  [3:0] a1,
  input  [3:0] a2,
  input  [3:0] a3,
  input  [3:0] a4,
  output [3:0] out_5,
  output out_6
);

  wire [3:0] bit_extender_1_out, bit_extender_2_out, multiplier_1_out, multiplier_2_out, subtractor_1_out,
       xor_1_out;

  Multiplier #(.width(4)) multiplier_1 (.a(a1), .b(a4), .out(multiplier_1_out));  // open: cin, cout
  Multiplier #(.width(4)) multiplier_2 (.a(a2), .b(a3), .out(multiplier_2_out));  // open: cin, cout
  Comparator #(.width(4), .mode("unsigned")) comparator_1 (
    .a(multiplier_1_out), .b(multiplier_2_out), .lt(out_6));  // open: gt, eq
  Subtractor #(.width(4)) subtractor_1 (
    .a(multiplier_1_out), .b(multiplier_2_out), .out(subtractor_1_out));  // open: bin, bout
  assign bit_extender_1_out = {{3{out_6}}, out_6};  // Bit_Extender bit_extender_1
  assign xor_1_out = subtractor_1_out ^ bit_extender_1_out;  // XOR_Gate xor_1, 4 bits wide
  assign bit_extender_2_out = {{3{1'b0}}, out_6};  // Bit_Extender bit_extender_2
  Adder_part #(.width(4)) adder_1 (.a(xor_1_out), .b(bit_extender_2_out), .out(out_5));  // open: cin, cout
endmodule

module _7segment (
  input  D,
  input  C,
  input  B,
  input  A,
  output a_2,
  output b_2,
  output c_2,
  output d_2,
  output e,
  output f,
  output g
);

  wire and_1_out, and_2_out, and_3_out, and_4_out, and_5_out, and_6_out, and_7_out, and_8_out, and_9_out,
       and_10_out, and_11_out, and_12_out, and_13_out, and_14_out, and_15_out, and_16_out, and_17_out,
       not_1_out, not_2_out, not_3_out, not_4_out, not_5_out, not_6_out, not_7_out, not_8_out, not_9_out,
       not_10_out, not_11_out, not_12_out, not_13_out, not_14_out, not_15_out, not_16_out, not_17_out,
       not_18_out, not_19_out, not_20_out, not_21_out, or_1_out, or_2_out, or_3_out, or_4_out, or_6_out,
       or_8_out, or_9_out, or_10_out, or_11_out, or_14_out, or_15_out;

  not not_1 (not_1_out, C);
  and and_1 (and_1_out, not_1_out, not_2_out);
  not not_2 (not_2_out, A);
  and and_2 (and_2_out, C, A);
  not not_3 (not_3_out, C);
  not not_4 (not_4_out, B);
  and and_3 (and_3_out, not_4_out, not_5_out);
  not not_5 (not_5_out, A);
  not not_6 (not_6_out, B);
  or or_1 (or_1_out, not_6_out, A);
  not not_7 (not_7_out, C);
  and and_4 (and_4_out, not_7_out, not_8_out);
  not not_8 (not_8_out, A);
  not not_9 (not_9_out, C);
  and and_5 (and_5_out, not_9_out, B);
  not not_10 (not_10_out, A);
  and and_6 (and_6_out, C, not_11_out);
  not not_11 (not_11_out, B);
  not not_12 (not_12_out, C);
  and and_7 (and_7_out, not_12_out, not_13_out);
  not not_13 (not_13_out, A);
  and and_8 (and_8_out, B, not_14_out);
  not not_14 (not_14_out, A);
  not not_15 (not_15_out, B);
  and and_9 (and_9_out, not_15_out, not_16_out);
  not not_16 (not_16_out, A);
  and and_10 (and_10_out, C, not_17_out);
  not not_17 (not_17_out, B);
  and and_11 (and_11_out, C, not_18_out);
  not not_18 (not_18_out, A);
  not not_19 (not_19_out, C);
  and and_12 (and_12_out, not_19_out, B);
  and and_13 (and_13_out, C, not_20_out);
  not not_20 (not_20_out, B);
  and and_14 (and_14_out, C, not_21_out);
  not not_21 (not_21_out, A);
  or or_2 (or_2_out, and_1_out, B);
  or or_3 (or_3_out, and_2_out, D);
  or or_4 (or_4_out, not_3_out, and_3_out);
  and and_15 (and_15_out, B, A);
  or or_5 (c_2, or_1_out, C);
  or or_6 (or_6_out, and_4_out, and_5_out);
  and and_16 (and_16_out, B, not_10_out);
  and and_17 (and_17_out, and_6_out, A);
  or or_7 (e, and_7_out, and_8_out);
  or or_8 (or_8_out, and_9_out, and_10_out);
  or or_9 (or_9_out, and_11_out, D);
  or or_10 (or_10_out, and_12_out, and_13_out);
  or or_11 (or_11_out, and_14_out, D);
  or or_12 (a_2, or_2_out, or_3_out);
  or or_13 (b_2, or_4_out, and_15_out);
  or or_14 (or_14_out, or_6_out, and_16_out);
  or or_15 (or_15_out, and_17_out, D);
  or or_16 (f, or_8_out, or_9_out);
  or or_17 (g, or_10_out, or_11_out);
  or or_18 (d_2, or_14_out, or_15_out);
endmodule

// ScalarX
module Scalar_multiplier (
  input  [3:0] in_1,
  input  [3:0] in_2,
  input  [3:0] in_3,
  input  [3:0] in_4,
  input  [3:0] in_5,
  output [3:0] out_6,
  output [3:0] out_7,
  output [3:0] out_8,
  output [3:0] out_9
);

  Multiplier #(.width(4)) multiplier_1 (.a(in_2), .b(in_1), .out(out_6));  // open: cin, cout
  Multiplier #(.width(4)) multiplier_2 (.a(in_3), .b(in_1), .out(out_7));  // open: cin, cout
  Multiplier #(.width(4)) multiplier_3 (.a(in_4), .b(in_1), .out(out_8));  // open: cin, cout
  Multiplier #(.width(4)) multiplier_4 (.a(in_5), .b(in_1), .out(out_9));  // open: cin, cout
endmodule

// Matrix-X
module Matrix_Mulitplier (
  input  [3:0] a1,
  input  [3:0] a2,
  input  [3:0] a3,
  input  [3:0] a4,
  input  [3:0] b1,
  input  [3:0] b2,
  input  [3:0] b3,
  input  [3:0] b4,
  output [3:0] out_9,
  output [3:0] out_10,
  output [3:0] out_11,
  output [3:0] out_12
);

  wire [3:0] multiplier_1_out, multiplier_2_out, multiplier_3_out, multiplier_4_out, multiplier_5_out,
       multiplier_6_out, multiplier_7_out, multiplier_8_out;

  Multiplier #(.width(4)) multiplier_1 (.a(a1), .b(b1), .out(multiplier_1_out));  // open: cin, cout
  Multiplier #(.width(4)) multiplier_2 (.a(a2), .b(b3), .out(multiplier_2_out));  // open: cin, cout
  Multiplier #(.width(4)) multiplier_3 (.a(a1), .b(b2), .out(multiplier_3_out));  // open: cin, cout
  Multiplier #(.width(4)) multiplier_4 (.a(a2), .b(b4), .out(multiplier_4_out));  // open: cin, cout
  Multiplier #(.width(4)) multiplier_5 (.a(a3), .b(b1), .out(multiplier_5_out));  // open: cin, cout
  Multiplier #(.width(4)) multiplier_6 (.a(a4), .b(b3), .out(multiplier_6_out));  // open: cin, cout
  Multiplier #(.width(4)) multiplier_7 (.a(a3), .b(b2), .out(multiplier_7_out));  // open: cin, cout
  Multiplier #(.width(4)) multiplier_8 (.a(a4), .b(b4), .out(multiplier_8_out));  // open: cin, cout
  Adder_part #(.width(4)) adder_1 (.a(multiplier_1_out), .b(multiplier_2_out), .out(out_9));  // open: cin, cout
  Adder_part #(.width(4)) adder_2 (.a(multiplier_3_out), .b(multiplier_4_out), .out(out_10));  // open: cin, cout
  Adder_part #(.width(4)) adder_3 (.a(multiplier_5_out), .b(multiplier_6_out), .out(out_11));  // open: cin, cout
  Adder_part #(.width(4)) adder_4 (.a(multiplier_7_out), .b(multiplier_8_out), .out(out_12));  // open: cin, cout
endmodule

module Transpose (
  input  [3:0] a1,
  input  [3:0] a2,
  input  [3:0] a3,
  input  [3:0] a4,
  output [3:0] out_5,
  output [3:0] out_6,
  output [3:0] out_7,
  output [3:0] out_8
);


  assign out_5 = a1;
  assign out_6 = a3;
  assign out_7 = a2;
  assign out_8 = a4;
endmodule

module Inverse (
  input  [3:0] a1,
  input  [3:0] a2,
  input  [3:0] a3,
  input  [3:0] a4,
  output [3:0] b1,
  output nb2,
  output [3:0] b2,
  output nb3,
  output [3:0] b3,
  output [3:0] b4
);

  wire comparator_1_eq, not_1_out;
  wire [3:0] bit_extender_1_out, determinant_1_out_5;

  Determinant determinant_1 (.a1(a1), .a2(a2), .a3(a3), .a4(a4), .out_5(determinant_1_out_5));  // open: out_6
  not not_1 (not_1_out, comparator_1_eq);
  Comparator #(.width(4), .mode("unsigned")) comparator_1 (
    .a(determinant_1_out_5), .b(4'b0000), .eq(comparator_1_eq));  // open: gt, lt
  assign bit_extender_1_out = {{3{not_1_out}}, not_1_out};  // Bit_Extender bit_extender_1
  assign b4 = a1 & bit_extender_1_out;  // AND_Gate and_1, 4 bits wide
  assign b2 = a2 & bit_extender_1_out;  // AND_Gate and_2, 4 bits wide
  assign b3 = a3 & bit_extender_1_out;  // AND_Gate and_3, 4 bits wide
  assign b1 = a4 & bit_extender_1_out;  // AND_Gate and_4, 4 bits wide

  assign nb2 = 1'b1;
  assign nb3 = 1'b1;
endmodule

// Subtractor
module Sub (
  input  [3:0] a1,
  input  [3:0] b1,
  input  [3:0] a2,
  input  [3:0] b2,
  input  [3:0] a3,
  input  [3:0] b3,
  input  [3:0] a4,
  input  [3:0] b4,
  output [3:0] out_9,
  output out_10,
  output [3:0] out_11,
  output out_12,
  output [3:0] out_13,
  output out_14,
  output [3:0] out_15,
  output out_16
);

  wire [3:0] bit_extender_1_out, bit_extender_2_out, bit_extender_3_out, bit_extender_4_out,
       bit_extender_5_out, bit_extender_6_out, bit_extender_7_out, bit_extender_8_out, subtractor_1_out,
       subtractor_2_out, subtractor_3_out, subtractor_4_out, xor_1_out, xor_2_out, xor_3_out, xor_4_out;

  Comparator #(.width(4), .mode("unsigned")) comparator_1 (.a(a1), .b(b1), .lt(out_10));  // open: gt, eq
  Comparator #(.width(4), .mode("unsigned")) comparator_2 (.a(a2), .b(b2), .lt(out_12));  // open: gt, eq
  Comparator #(.width(4), .mode("unsigned")) comparator_3 (.a(a3), .b(b3), .lt(out_14));  // open: gt, eq
  Comparator #(.width(4), .mode("unsigned")) comparator_4 (.a(a4), .b(b4), .lt(out_16));  // open: gt, eq
  assign bit_extender_1_out = {{3{out_10}}, out_10};  // Bit_Extender bit_extender_1
  assign bit_extender_2_out = {{3{out_12}}, out_12};  // Bit_Extender bit_extender_2
  assign bit_extender_3_out = {{3{out_14}}, out_14};  // Bit_Extender bit_extender_3
  assign bit_extender_4_out = {{3{out_16}}, out_16};  // Bit_Extender bit_extender_4
  Subtractor #(.width(4)) subtractor_1 (.a(a1), .b(b1), .out(subtractor_1_out));  // open: bin, bout
  Subtractor #(.width(4)) subtractor_2 (.a(a2), .b(b2), .out(subtractor_2_out));  // open: bin, bout
  Subtractor #(.width(4)) subtractor_3 (.a(a3), .b(b3), .out(subtractor_3_out));  // open: bin, bout
  Subtractor #(.width(4)) subtractor_4 (.a(a4), .b(b4), .out(subtractor_4_out));  // open: bin, bout
  assign xor_1_out = subtractor_1_out ^ bit_extender_1_out;  // XOR_Gate xor_1, 4 bits wide
  assign xor_2_out = subtractor_2_out ^ bit_extender_2_out;  // XOR_Gate xor_2, 4 bits wide
  assign xor_3_out = subtractor_3_out ^ bit_extender_3_out;  // XOR_Gate xor_3, 4 bits wide
  assign xor_4_out = subtractor_4_out ^ bit_extender_4_out;  // XOR_Gate xor_4, 4 bits wide
  assign bit_extender_5_out = {{3{1'b0}}, out_10};  // Bit_Extender bit_extender_5
  assign bit_extender_6_out = {{3{1'b0}}, out_12};  // Bit_Extender bit_extender_6
  assign bit_extender_7_out = {{3{1'b0}}, out_14};  // Bit_Extender bit_extender_7
  assign bit_extender_8_out = {{3{1'b0}}, out_16};  // Bit_Extender bit_extender_8
  Adder_part #(.width(4)) adder_1 (.a(xor_1_out), .b(bit_extender_5_out), .out(out_9));  // open: cin, cout
  Adder_part #(.width(4)) adder_2 (.a(xor_2_out), .b(bit_extender_6_out), .out(out_11));  // open: cin, cout
  Adder_part #(.width(4)) adder_3 (.a(xor_3_out), .b(bit_extender_7_out), .out(out_13));  // open: cin, cout
  Adder_part #(.width(4)) adder_4 (.a(xor_4_out), .b(bit_extender_8_out), .out(out_15));  // open: cin, cout
endmodule

module Main (
  input  [2:0] Operation,
  input  [3:0] Input_1,
  input  [3:0] Input_2,
  input  [3:0] Input_3,
  input  [3:0] Input_4,
  input  [3:0] Scalar_Multiplier
);

  wire Control_out, determinant_1_out_6, inverse_1_nb2, inverse_1_nb3, multiplexer_3_out, multiplexer_4_out,
       multiplexer_7_out, multiplexer_8_out, n7segment_1_a_2, n7segment_1_b_2, n7segment_1_c_2,
       n7segment_1_d_2, n7segment_1_e, n7segment_1_f, n7segment_1_g, n7segment_2_a_2, n7segment_2_b_2,
       n7segment_2_c_2, n7segment_2_d_2, n7segment_2_e, n7segment_2_f, n7segment_2_g, n7segment_3_a_2,
       n7segment_3_b_2, n7segment_3_c_2, n7segment_3_d_2, n7segment_3_e, n7segment_3_f, n7segment_3_g,
       n7segment_4_a_2, n7segment_4_b_2, n7segment_4_c_2, n7segment_4_d_2, n7segment_4_e, n7segment_4_f,
       n7segment_4_g, sub_1_out_10, sub_1_out_12, sub_1_out_14, sub_1_out_16;
  wire [3:0] adder_1_c1, adder_1_c2, adder_1_c3, adder_1_c4, determinant_1_out_5, inverse_1_b1, inverse_1_b2,
       inverse_1_b3, inverse_1_b4, matrix_mulitplier_1_out_9, matrix_mulitplier_1_out_10,
       matrix_mulitplier_1_out_11, matrix_mulitplier_1_out_12, multiplexer_1_out, multiplexer_2_out,
       multiplexer_5_out, multiplexer_6_out, scalar_multiplier_1_out_6, scalar_multiplier_1_out_7,
       scalar_multiplier_1_out_8, scalar_multiplier_1_out_9, storage_1__021, storage_1_o11, storage_1_o12,
       storage_1_o22, storage_1_o31, storage_1_o32, storage_1_o41, storage_1_o42, sub_1_out_9, sub_1_out_11,
       sub_1_out_13, sub_1_out_15, transpose_1_out_5, transpose_1_out_6, transpose_1_out_7, transpose_1_out_8;

  Button Control (.out(Control_out));
  Storage storage_1 (
    .a1(Input_1), .a2(Input_2), .a3(Input_3), .a4(Input_4), .o12(storage_1_o12), .o11(storage_1_o11),
    .o22(storage_1_o22), ._021(storage_1__021), .o32(storage_1_o32), .o31(storage_1_o31),
    .o42(storage_1_o42), .o41(storage_1_o41), .Control(Control_out));
  Adder adder_1 (
    .a1(storage_1_o11), .b1(storage_1_o12), .a2(storage_1__021), .b2(storage_1_o22), .a3(storage_1_o31),
    .b3(storage_1_o32), .a4(storage_1_o41), .b4(storage_1_o42), .c1(adder_1_c1), .c2(adder_1_c2),
    .c3(adder_1_c3), .c4(adder_1_c4));
  Matrix_Mulitplier matrix_mulitplier_1 (
    .a1(storage_1_o11), .a2(storage_1__021), .a3(storage_1_o31), .a4(storage_1_o41), .b1(storage_1_o12),
    .b2(storage_1_o22), .b3(storage_1_o32), .b4(storage_1_o42), .out_9(matrix_mulitplier_1_out_9),
    .out_10(matrix_mulitplier_1_out_10), .out_11(matrix_mulitplier_1_out_11),
    .out_12(matrix_mulitplier_1_out_12));
  Scalar_multiplier scalar_multiplier_1 (
    .in_1(Scalar_Multiplier), .in_2(storage_1_o11), .in_3(storage_1__021), .in_4(storage_1_o31),
    .in_5(storage_1_o41), .out_6(scalar_multiplier_1_out_6), .out_7(scalar_multiplier_1_out_7),
    .out_8(scalar_multiplier_1_out_8), .out_9(scalar_multiplier_1_out_9));
  Transpose transpose_1 (
    .a1(storage_1_o11), .out_6(transpose_1_out_6), .a2(storage_1__021), .a3(storage_1_o31),
    .a4(storage_1_o41), .out_5(transpose_1_out_5), .out_7(transpose_1_out_7), .out_8(transpose_1_out_8));
  Determinant determinant_1 (
    .a1(storage_1_o11), .a2(storage_1__021), .a3(storage_1_o31), .a4(storage_1_o41),
    .out_5(determinant_1_out_5), .out_6(determinant_1_out_6));
  Inverse inverse_1 (
    .a1(storage_1_o11), .a2(storage_1__021), .a3(storage_1_o31), .a4(storage_1_o41), .b1(inverse_1_b1),
    .b2(inverse_1_b2), .b3(inverse_1_b3), .b4(inverse_1_b4), .nb2(inverse_1_nb2), .nb3(inverse_1_nb3));
  Sub sub_1 (
    .out_9(sub_1_out_9), .a1(storage_1_o11), .b1(storage_1_o12), .out_10(sub_1_out_10),
    .out_11(sub_1_out_11), .a2(storage_1__021), .b2(storage_1_o22), .out_12(sub_1_out_12),
    .out_13(sub_1_out_13), .a3(storage_1_o31), .b3(storage_1_o32), .out_14(sub_1_out_14),
    .out_15(sub_1_out_15), .a4(storage_1_o41), .b4(storage_1_o42), .out_16(sub_1_out_16));
  Multiplexer #(.select(3), .width(4)) multiplexer_1 (
    .in0(adder_1_c1), .in1(sub_1_out_9), .in2(matrix_mulitplier_1_out_9), .in3(scalar_multiplier_1_out_6),
    .in4(transpose_1_out_5), .in5(determinant_1_out_5), .in6(inverse_1_b1), .out(multiplexer_1_out),
    .sel(Operation));  // open: in7, en
  Multiplexer #(.select(3), .width(4)) multiplexer_2 (
    .in0(adder_1_c2), .in1(sub_1_out_11), .in2(matrix_mulitplier_1_out_10), .in3(scalar_multiplier_1_out_7),
    .in4(transpose_1_out_6), .in6(inverse_1_b2), .out(multiplexer_2_out), .sel(Operation));  // open: in5, in7, en
  Multiplexer #(.select(3)) multiplexer_3 (
    .in1(sub_1_out_10), .in5(determinant_1_out_6), .out(multiplexer_3_out), .sel(Operation));  // open: in0, in2, in3, in4, in6, in7, en
  Multiplexer #(.select(3)) multiplexer_4 (
    .in1(sub_1_out_14), .in6(inverse_1_nb3), .out(multiplexer_4_out), .sel(Operation));  // open: in0, in2, in3, in4, in5, in7, en
  Multiplexer #(.select(3), .width(4)) multiplexer_5 (
    .in0(adder_1_c3), .in1(sub_1_out_13), .in2(matrix_mulitplier_1_out_11), .in3(scalar_multiplier_1_out_8),
    .in4(transpose_1_out_7), .in6(inverse_1_b3), .out(multiplexer_5_out), .sel(Operation));  // open: in5, in7, en
  Multiplexer #(.select(3), .width(4)) multiplexer_6 (
    .in0(adder_1_c4), .in1(sub_1_out_15), .in2(matrix_mulitplier_1_out_12), .in3(scalar_multiplier_1_out_9),
    .in4(transpose_1_out_8), .in6(inverse_1_b4), .out(multiplexer_6_out), .sel(Operation));  // open: in5, in7, en
  Multiplexer #(.select(3)) multiplexer_7 (
    .in1(sub_1_out_12), .in6(inverse_1_nb2), .out(multiplexer_7_out), .sel(Operation));  // open: in0, in2, in3, in4, in5, in7, en
  Multiplexer #(.select(3)) multiplexer_8 (
    .in1(sub_1_out_16), .out(multiplexer_8_out), .sel(Operation));  // open: in0, in2, in3, in4, in5, in6, in7, en
  _7_Segment_Display u_7_segment_display_1 (.g(multiplexer_3_out));  // open: f, a, b, e, d, c, dp
  _7_Segment_Display u_7_segment_display_2 (.g(multiplexer_4_out));  // open: f, a, b, e, d, c, dp
  _7_Segment_Display u_7_segment_display_3 (
    .g(n7segment_1_g), .f(n7segment_1_f), .a(n7segment_1_a_2), .b(n7segment_1_b_2), .e(n7segment_1_e),
    .d(n7segment_1_d_2), .c(n7segment_1_c_2));  // open: dp
  _7_Segment_Display u_7_segment_display_4 (
    .g(n7segment_2_g), .f(n7segment_2_f), .a(n7segment_2_a_2), .b(n7segment_2_b_2), .e(n7segment_2_e),
    .d(n7segment_2_d_2), .c(n7segment_2_c_2));  // open: dp
  _7segment u_7segment_1 (
    .D(multiplexer_1_out[3]), .C(multiplexer_1_out[2]), .B(multiplexer_1_out[1]), .A(multiplexer_1_out[0]),
    .a_2(n7segment_1_a_2), .b_2(n7segment_1_b_2), .c_2(n7segment_1_c_2), .d_2(n7segment_1_d_2),
    .e(n7segment_1_e), .f(n7segment_1_f), .g(n7segment_1_g));
  _7segment u_7segment_2 (
    .D(multiplexer_5_out[3]), .C(multiplexer_5_out[2]), .B(multiplexer_5_out[1]), .A(multiplexer_5_out[0]),
    .a_2(n7segment_2_a_2), .b_2(n7segment_2_b_2), .c_2(n7segment_2_c_2), .d_2(n7segment_2_d_2),
    .e(n7segment_2_e), .f(n7segment_2_f), .g(n7segment_2_g));
  _7_Segment_Display u_7_segment_display_5 (.g(multiplexer_7_out));  // open: f, a, b, e, d, c, dp
  _7_Segment_Display u_7_segment_display_6 (.g(multiplexer_8_out));  // open: f, a, b, e, d, c, dp
  _7_Segment_Display u_7_segment_display_7 (
    .g(n7segment_3_g), .f(n7segment_3_f), .a(n7segment_3_a_2), .b(n7segment_3_b_2), .e(n7segment_3_e),
    .d(n7segment_3_d_2), .c(n7segment_3_c_2));  // open: dp
  _7_Segment_Display u_7_segment_display_8 (
    .g(n7segment_4_g), .f(n7segment_4_f), .a(n7segment_4_a_2), .b(n7segment_4_b_2), .e(n7segment_4_e),
    .d(n7segment_4_d_2), .c(n7segment_4_c_2));  // open: dp
  _7segment u_7segment_3 (
    .D(multiplexer_2_out[3]), .C(multiplexer_2_out[2]), .B(multiplexer_2_out[1]), .A(multiplexer_2_out[0]),
    .a_2(n7segment_3_a_2), .b_2(n7segment_3_b_2), .c_2(n7segment_3_c_2), .d_2(n7segment_3_d_2),
    .e(n7segment_3_e), .f(n7segment_3_f), .g(n7segment_3_g));
  _7segment u_7segment_4 (
    .D(multiplexer_6_out[3]), .C(multiplexer_6_out[2]), .B(multiplexer_6_out[1]), .A(multiplexer_6_out[0]),
    .a_2(n7segment_4_a_2), .b_2(n7segment_4_b_2), .c_2(n7segment_4_c_2), .d_2(n7segment_4_d_2),
    .e(n7segment_4_e), .f(n7segment_4_f), .g(n7segment_4_g));
endmodule

module Storage (
  input  Control,
  input  [3:0] a1,
  input  [3:0] a2,
  input  [3:0] a3,
  input  [3:0] a4,
  output [3:0] o12,
  output [3:0] o11,
  output [3:0] o22,
  output [3:0] _021,
  output [3:0] o32,
  output [3:0] o31,
  output [3:0] o42,
  output [3:0] o41
);

  D_Flip_Flop d_ff_1 (.clk(Control), .D(a1[0]), .Q(o11[0]), .en(1'b1));  // open: Qn, preset, reset
  D_Flip_Flop d_ff_2 (.clk(Control), .D(a1[1]), .Q(o11[1]), .en(1'b1));  // open: Qn, preset, reset
  D_Flip_Flop d_ff_3 (.clk(Control), .D(a1[2]), .Q(o11[2]), .en(1'b1));  // open: Qn, preset, reset
  D_Flip_Flop d_ff_4 (.clk(Control), .D(a1[3]), .Q(o11[3]), .en(1'b1));  // open: Qn, preset, reset
  D_Flip_Flop d_ff_5 (.clk(Control), .D(a2[0]), .Q(_021[0]), .en(1'b1));  // open: Qn, preset, reset
  D_Flip_Flop d_ff_6 (.clk(Control), .D(a2[1]), .Q(_021[1]), .en(1'b1));  // open: Qn, preset, reset
  D_Flip_Flop d_ff_7 (.clk(Control), .D(a2[2]), .Q(_021[2]), .en(1'b1));  // open: Qn, preset, reset
  D_Flip_Flop d_ff_8 (.clk(Control), .D(a2[3]), .Q(_021[3]), .en(1'b1));  // open: Qn, preset, reset
  D_Flip_Flop d_ff_9 (.clk(Control), .D(a3[0]), .Q(o31[0]), .en(1'b1));  // open: Qn, preset, reset
  D_Flip_Flop d_ff_10 (.clk(Control), .D(a3[1]), .Q(o31[1]), .en(1'b1));  // open: Qn, preset, reset
  D_Flip_Flop d_ff_11 (.clk(Control), .D(a3[2]), .Q(o31[2]), .en(1'b1));  // open: Qn, preset, reset
  D_Flip_Flop d_ff_12 (.clk(Control), .D(a3[3]), .Q(o31[3]), .en(1'b1));  // open: Qn, preset, reset
  D_Flip_Flop d_ff_13 (.clk(Control), .D(a4[0]), .Q(o41[0]), .en(1'b1));  // open: Qn, preset, reset
  D_Flip_Flop d_ff_14 (.clk(Control), .D(a4[1]), .Q(o41[1]), .en(1'b1));  // open: Qn, preset, reset
  D_Flip_Flop d_ff_15 (.clk(Control), .D(a4[2]), .Q(o41[2]), .en(1'b1));  // open: Qn, preset, reset
  D_Flip_Flop d_ff_16 (.clk(Control), .D(a4[3]), .Q(o41[3]), .en(1'b1));  // open: Qn, preset, reset

  assign o12 = a1;
  assign o22 = a2;
  assign o32 = a3;
  assign o42 = a4;
endmodule
